// Digital circuit alu_32.dig as structural Verilog
module alu_32 (
  input  [34:0] ALU_OP,
  input  [31:0] DIN,
  input  CLK,
  input  WRITE_A,
  input  WRITE_B,
  input  [31:0] X,
  input  [31:0] Y,
  input  SENSE,
  output [31:0] DOUT,
  output TEST
);

  wire comparator_1_eq, comparator_2_eq, comparator_3_eq, comparator_3_gt, comparator_3_lt,
       multiplexer_3_out, not_2_out;
  wire [31:0] add_1_s, and_1_out, multiplexer_1_out, multiplexer_2_out, not_1_out, or_1_out, REG_ALU_A_q,
       REG_ALU_B_q, xor_1_out;

  Register #(.Bits(32)) REG_ALU_A (.D(DIN), .C(CLK), .en(WRITE_A), .Q(REG_ALU_A_q));
  Register #(.Bits(32)) REG_ALU_B (.D(DIN), .C(CLK), .en(WRITE_B), .Q(REG_ALU_B_q));
  Multiplexer #(.Selector_Bits(2), .Bits(32)) multiplexer_1 (
    .sel(ALU_OP[6:5]), .in_0(REG_ALU_B_q), .in_1({{5{1'b0}}, ALU_OP[33:7]}),
    .in_2({1'b0, REG_ALU_B_q[31:1]}), .in_3({REG_ALU_B_q[30:0], 1'b0}), .out(multiplexer_1_out));
  assign not_1_out = ~multiplexer_1_out;  // Not not_1, 32 bits wide
  Multiplexer #(.Bits(32)) multiplexer_2 (
    .sel(ALU_OP[3]), .in_0(multiplexer_1_out), .in_1(not_1_out), .out(multiplexer_2_out));
  Comparator #(.Bits(32)) comparator_1 (.a({32{1'b0}}), .b(REG_ALU_A_q), .eq(comparator_1_eq));  // open: gt, lt
  Comparator #(.Bits(32)) comparator_2 (.a({32{1'b0}}), .b(multiplexer_2_out), .eq(comparator_2_eq));  // open: gt, lt
  Comparator #(.Bits(32)) comparator_3 (
    .a(REG_ALU_A_q), .b(multiplexer_2_out), .gt(comparator_3_gt), .eq(comparator_3_eq), .lt(comparator_3_lt));
  Add #(.Bits(32)) add_1 (.a(REG_ALU_A_q), .b(multiplexer_2_out), .c_i(ALU_OP[4]), .s(add_1_s));  // open: c_o
  assign and_1_out = REG_ALU_A_q & multiplexer_2_out;  // And and_1, 32 bits wide
  assign or_1_out = REG_ALU_A_q | multiplexer_2_out;  // Or or_1, 32 bits wide
  assign xor_1_out = REG_ALU_A_q ^ multiplexer_2_out;  // XOr xor_1, 32 bits wide
  Multiplexer #(.Selector_Bits(3)) multiplexer_3 (
    .sel(ALU_OP[2:0]), .in_0(comparator_1_eq), .in_1(comparator_2_eq), .in_2(comparator_3_gt),
    .in_3(comparator_3_eq), .in_4(comparator_3_lt), .in_5(multiplexer_2_out[0]),
    .in_6(multiplexer_2_out[31]), .in_7(SENSE), .out(multiplexer_3_out));
  Multiplexer #(.Selector_Bits(3), .Bits(32)) multiplexer_4 (
    .sel(ALU_OP[2:0]), .in_0(add_1_s), .in_1(and_1_out), .in_2(or_1_out), .in_3(xor_1_out),
    .in_4(REG_ALU_A_q), .in_5(multiplexer_2_out), .in_6(X), .in_7(Y), .out(DOUT));
  not not_2 (not_2_out, multiplexer_3_out);
  Multiplexer multiplexer_5 (.sel(ALU_OP[3]), .in_0(multiplexer_3_out), .in_1(not_2_out), .out(TEST));
endmodule
