// Digital circuit alu_slice.dig as structural Verilog
module alu_slice (
  input  CLK,
  input  DIN,
  input  WRITE_A,
  input  WRITE_B,
  input  [6:0] ALU_OP,
  input  ALU_IMM,
  input  X,
  input  Y,
  input  ADD_CIN,
  input  AZ_IN,
  input  BZ_IN,
  input  BP_IN,
  input  BN_IN,
  input  GT_IN,
  input  LT_IN,
  input  EQ_IN,
  output DOUT,
  output ADD_COUT,
  output AZ_OUT,
  output BZ_OUT,
  output B_OUT,
  output GT_OUT,
  output EQ_OUT,
  output LT_OUT
);

  wire add_1_s, and_1_out, and_2_out, and_3_out, and_4_out, and_6_out, multiplexer_1_out, multiplexer_2_out,
       not_1_out, or_3_out, REG_ALU_A_q, xnor_1_out, xor_1_out;

  Register REG_ALU_A (.D(DIN), .C(CLK), .en(WRITE_A), .Q(REG_ALU_A_q));
  Register REG_ALU_B (.D(DIN), .C(CLK), .en(WRITE_B), .Q(B_OUT));
  Multiplexer #(.Selector_Bits(2)) multiplexer_1 (
    .sel(ALU_OP[6:5]), .in_0(B_OUT), .in_1(ALU_IMM), .in_2(BP_IN), .in_3(BN_IN), .out(multiplexer_1_out));
  not not_1 (not_1_out, multiplexer_1_out);
  Multiplexer multiplexer_2 (.sel(ALU_OP[3]), .in_0(multiplexer_1_out), .in_1(not_1_out), .out(multiplexer_2_out));
  or or_1 (AZ_OUT, AZ_IN, REG_ALU_A_q);
  or or_2 (BZ_OUT, BZ_IN, multiplexer_2_out);
  and and_1 (and_1_out, REG_ALU_A_q, ~multiplexer_2_out);  // And
  xnor xnor_1 (xnor_1_out, REG_ALU_A_q, multiplexer_2_out);
  and and_2 (and_2_out, ~REG_ALU_A_q, multiplexer_2_out);  // And
  Add add_1 (.a(REG_ALU_A_q), .b(multiplexer_2_out), .c_i(ADD_CIN), .s(add_1_s), .c_o(ADD_COUT));
  and and_3 (and_3_out, REG_ALU_A_q, multiplexer_2_out);
  or or_3 (or_3_out, REG_ALU_A_q, multiplexer_2_out);
  xor xor_1 (xor_1_out, REG_ALU_A_q, multiplexer_2_out);
  and and_4 (and_4_out, GT_IN, xnor_1_out);
  and and_5 (EQ_OUT, xnor_1_out, EQ_IN);
  and and_6 (and_6_out, xnor_1_out, LT_IN);
  or or_4 (GT_OUT, and_1_out, and_4_out);
  or or_5 (LT_OUT, and_6_out, and_2_out);
  Multiplexer #(.Selector_Bits(3)) multiplexer_3 (
    .sel(ALU_OP[2:0]), .in_0(add_1_s), .in_1(and_3_out), .in_2(or_3_out), .in_3(xor_1_out),
    .in_4(REG_ALU_A_q), .in_5(multiplexer_2_out), .in_6(X), .in_7(Y), .out(DOUT));
endmodule
