// Digital circuit mcpu_core.dig as structural Verilog
module mcpu_core (
  input  [7:0] ROM_VALUE,
  input  CLK,
  input  [31:0] DIN,
  input  [31:0] X,
  input  [31:0] Y,
  input  SENSE,
  output [31:0] RAM_ADDR,
  output [31:0] DOUT,
  output RAM_WRITE,
  output RAM_UPDATE,
  output RAM_READ,
  output TARGET_I,
  output TARGET_J,
  output TARGET_K,
  output SOURCE_I,
  output SOURCE_J,
  output SOURCE_K,
  output [31:0] ROM_ADDR,
  output HALTED
);

  wire alu_32_1_test, op_decode_32_1_op_isimm, OP_SOURCE_ADDR, OP_SOURCE_ALU, OP_SOURCE_IMM, OP_SOURCE_PC,
       OP_TARGET_ALU_A, OP_TARGET_ALU_B, OP_TARGET_PC;
  wire [31:0] alu_32_1_dout;
  wire [34:0] op_decode_32_1_imm_35;

  op_decode_32 op_decode_32_1 (
    .CLK(CLK), .OP_CODE(ROM_VALUE), .TEST(alu_32_1_test),
    .OP_SOURCE({SOURCE_K, SOURCE_J, SOURCE_I, OP_SOURCE_ALU, OP_SOURCE_IMM, RAM_READ, OP_SOURCE_ADDR, OP_SOURCE_PC}),
    .OP_TARGET({TARGET_K, TARGET_J, TARGET_I, OP_TARGET_ALU_B, OP_TARGET_ALU_A, RAM_WRITE, RAM_UPDATE, OP_TARGET_PC}),
    .IMM_35(op_decode_32_1_imm_35), .OP_ISIMM(op_decode_32_1_op_isimm));
  CounterPreset #(.Bits(32), .isProgramCounter("true")) CNT_PC (
    .en(1'b1), .C(CLK), .dir(1'b0), .in(DIN), .ld(OP_TARGET_PC), .clr(1'b0), .out(ROM_ADDR));  // open: ovf
  Register #(.Bits(32)) REG_ADDR (.D(DIN), .C(CLK), .en(RAM_UPDATE), .Q(RAM_ADDR));
  alu_32 alu_32_1 (
    .ALU_OP(op_decode_32_1_imm_35), .DIN(DIN), .CLK(CLK), .WRITE_A(OP_TARGET_ALU_B),
    .WRITE_B(OP_TARGET_ALU_A), .X(X), .Y(Y), .SENSE(SENSE), .DOUT(alu_32_1_dout), .TEST(alu_32_1_test));
  assign DIN = OP_SOURCE_IMM ? op_decode_32_1_imm_35[31:0] : 32'bz;  // Driver driver_1
  assign DIN = OP_SOURCE_PC ? ROM_ADDR : 32'bz;  // Driver driver_2
  assign DIN = OP_SOURCE_ADDR ? RAM_ADDR : 32'bz;  // Driver driver_3
  assign DIN = OP_SOURCE_ALU ? alu_32_1_dout : 32'bz;  // Driver driver_4
  and and_1 (HALTED, ~op_decode_32_1_op_isimm, OP_SOURCE_PC, OP_TARGET_PC);  // And
  // Probe OP_SOURCE on {SOURCE_K, SOURCE_J, SOURCE_I, OP_SOURCE_ALU, OP_SOURCE_IMM, RAM_READ, OP_SOURCE_ADDR, OP_SOURCE_PC}
  // Probe OP_TARGET on {TARGET_K, TARGET_J, TARGET_I, OP_TARGET_ALU_B, OP_TARGET_ALU_A, RAM_WRITE, RAM_UPDATE, OP_TARGET_PC}

  assign DOUT = DIN;

  // Other names for the same wires on the sheet: OP_TARGET_ADDR = RAM_UPDATE
endmodule
