// Digital circuit mcpu_core_slice.dig as structural Verilog
module mcpu_core_slice (
  input  PC_CIN,
  input  ADD_CIN,
  input  AZ_IN,
  input  BZ_IN,
  input  GT_IN,
  input  EQ_IN,
  input  LT_IN,
  input  BP_IN,
  input  BN_IN,
  input  [31:0] DIN,
  input  [31:0] IMM,
  input  ALU_OP,
  input  ALU_X,
  input  ALU_Y,
  input  ALU_IMM,
  input  OP_SOURCE_PC,
  input  OP_SOURCE_ADDR,
  input  OP_SOURCE_IMM,
  input  OP_SOURCE_ALU,
  input  OP_TARGET_PC,
  input  OP_TARGET_ADDR,
  input  OP_TARGET_ALU_A,
  input  OP_TARGET_ALU_B,
  input  CLK,
  output PC_COUT,
  output ADD_COUT,
  output AZ_OUT,
  output BZ_OUT,
  output GT_OUT,
  output EQ_OUT,
  output LT_OUT,
  output B_OUT,
  output [31:0] DOUT,
  output [31:0] ROM_ADDR,
  output [31:0] RAM_ADDR
);

  wire add_1_s, multiplexer_1_out;
  wire [31:0] alu_slice_1_p17;

  Multiplexer multiplexer_1 (.sel(OP_TARGET_PC), .in_0(add_1_s), .in_1(DIN[0]), .out(multiplexer_1_out));
  Register CNT_PC (.D(multiplexer_1_out), .C(CLK), .en(1'b1), .Q(ROM_ADDR[0]));
  Register REG_ADDR (.D(DIN[0]), .C(CLK), .en(OP_TARGET_ADDR), .Q(RAM_ADDR[0]));
  // alu_slice alu_slice_1: pin names not known; wires that end beside it: CLK, DIN, OP_TARGET_ALU_A, OP_TARGET_ALU_B, ALU_OP, ALU_IMM, ALU_X, ALU_Y, ADD_CIN, AZ_IN, BZ_IN, BP_IN, BN_IN, GT_IN, LT_IN, EQ_IN, alu_slice_1_p17, ADD_COUT, AZ_OUT, BZ_OUT, B_OUT, GT_OUT, EQ_OUT, LT_OUT
  Add add_1 (.a(PC_CIN), .b(ROM_ADDR[0]), .c_i(1'b0), .s(add_1_s), .c_o(PC_COUT));
  assign DIN = OP_SOURCE_IMM ? IMM : 32'bz;  // Driver driver_1
  assign DIN = OP_SOURCE_PC ? ROM_ADDR : 32'bz;  // Driver driver_2
  assign DIN = OP_SOURCE_ADDR ? RAM_ADDR : 32'bz;  // Driver driver_3
  assign DIN = OP_SOURCE_ALU ? alu_slice_1_p17 : 32'bz;  // Driver driver_4
  // Pins of 1 and 32 bits meet at DIN
  // Pins of 1 and 32 bits meet at ROM_ADDR
  // Pins of 1 and 32 bits meet at IMM
  // Pins of 1 and 32 bits meet at RAM_ADDR

  assign DOUT = DIN;
endmodule
