// Digital circuit mcpu_soc.dig as structural Verilog
module mcpu_soc (
  input  CLK
);

  wire ALU_TEST, and_1_out, OP_IS_IMM, OP_SOURCE_ADDR, OP_SOURCE_ALU, OP_SOURCE_IMM, OP_SOURCE_PC,
       OP_TARGET_ADDR, OP_TARGET_ALU_A, OP_TARGET_ALU_B, OP_TARGET_PC, RAM_READ, RAM_WRITE, SOURCE_I,
       TARGET_I;
  wire [7:0] ROM_VALUE;
  wire [7:6] op_decode_32_1_op_source, op_decode_32_1_op_target;
  wire [15:0] keyboard_1_d;
  wire [31:0] alu_32_1_dout, DIN, RAM_ADDR, ramdualaccess_1_d1, ROM_ADDR;
  wire [31:8] ramdualaccess_1_d2;
  wire [34:0] IMM_35;

  op_decode_32 op_decode_32_1 (
    .CLK(CLK), .OP_CODE(ROM_VALUE), .TEST(ALU_TEST),
    .OP_SOURCE({op_decode_32_1_op_source, SOURCE_I, OP_SOURCE_ALU, OP_SOURCE_IMM, RAM_READ, OP_SOURCE_ADDR, OP_SOURCE_PC}),
    .OP_TARGET({op_decode_32_1_op_target, TARGET_I, OP_TARGET_ALU_B, OP_TARGET_ALU_A, RAM_WRITE, OP_TARGET_ADDR, OP_TARGET_PC}),
    .IMM_35(IMM_35), .OP_ISIMM(OP_IS_IMM));
  // Probe DATA_BUS on DIN
  // Probe IMM_35 on IMM_35
  CounterPreset #(.Bits(32), .isProgramCounter("true")) CNT_PC (
    .en(1'b1), .C(CLK), .dir(1'b0), .in(DIN), .ld(OP_TARGET_PC), .clr(1'b0), .out(ROM_ADDR));  // open: ovf
  Register #(.Bits(32)) REG_ADDR (.D(DIN), .C(CLK), .en(OP_TARGET_ADDR), .Q(RAM_ADDR));
  alu_32 alu_32_1 (
    .ALU_OP(IMM_35), .DIN(DIN), .CLK(CLK), .WRITE_A(OP_TARGET_ALU_A), .WRITE_B(OP_TARGET_ALU_B),
    .X({32{1'b0}}), .Y({32{1'b0}}), .SENSE(1'b0), .DOUT(alu_32_1_dout), .TEST(ALU_TEST));
  Break break_1 (.brk(OP_TARGET_PC));
  Break break_2 (.brk(OP_TARGET_ADDR));
  Break break_3 (.brk(RAM_WRITE));
  Break break_4 (.brk(OP_TARGET_ALU_A));
  Break break_5 (.brk(OP_TARGET_ALU_B));
  Break break_6 (.brk(TARGET_I));
  assign DIN = OP_SOURCE_IMM ? IMM_35[31:0] : 32'bz;  // Driver driver_1
  assign DIN = OP_SOURCE_PC ? ROM_ADDR : 32'bz;  // Driver driver_2
  assign DIN = OP_SOURCE_ADDR ? RAM_ADDR : 32'bz;  // Driver driver_3
  assign DIN = OP_SOURCE_ALU ? alu_32_1_dout : 32'bz;  // Driver driver_4
  // Probe ROM_ADDR on ROM_ADDR
  // Probe RAM_ADDR on RAM_ADDR
  // Probe ALU_RES on alu_32_1_dout
  Break break_7 (.brk(OP_SOURCE_PC));
  Break break_8 (.brk(OP_SOURCE_ADDR));
  Break break_9 (.brk(RAM_READ));
  Break break_10 (.brk(OP_SOURCE_IMM));
  Break break_11 (.brk(OP_SOURCE_ALU));
  Break break_12 (.brk(SOURCE_I));
  and and_1 (and_1_out, ~OP_IS_IMM, OP_SOURCE_PC, OP_TARGET_PC);  // And
  Break SINGLE_STEP (.brk(CLK));
  RAMDualAccess #(.AddrBits(24), .isProgramMemory("true"), .Bits(32)) ramdualaccess_1 (
    .str(RAM_WRITE), .C(CLK), .ld(1'b1), .A1(RAM_ADDR[23:0]), .Din1(DIN), .A2(ROM_ADDR[23:0]),
    .D1(ramdualaccess_1_d1), .D2({ramdualaccess_1_d2, ROM_VALUE}));
  Terminal #(.termWidth(80), .termHeight(24)) terminal_1 (.D(DIN[7:0]), .C(CLK), .en(TARGET_I));
  Keyboard keyboard_1 (.C(CLK), .en(SOURCE_I), .D(keyboard_1_d));  // open: av
  Break HALTED (.brk(and_1_out));
  assign DIN = RAM_READ ? ramdualaccess_1_d1 : 32'bz;  // Driver driver_5
  // Probe RAM_READ on ramdualaccess_1_d1
  // Probe INSTR on {ramdualaccess_1_d2, ROM_VALUE}
  // Probe CLK_COUNT on CLK
  assign DIN = SOURCE_I ? {{16{1'b0}}, keyboard_1_d} : 32'bz;  // Driver driver_6

  // Other names for the same wires on the sheet: DOUT[31:0] = DIN

  // Notes on the sheet:
  //   CLK: Hz: 2147483647
  //   Instruction decoder
  //   Bus
  //   Bus target enables
  //   Bus source enables
  //   Control
  //   RAM
  //   Serial
endmodule
