// Digital circuit mcpu_soc_minecraft.dig as structural Verilog
module mcpu_soc_minecraft (
  input  CLK
);

  wire ALU_TEST, and_1_out, and_2_out, OP_IS_IMM, OP_SOURCE_ADDR, OP_SOURCE_ALU, OP_SOURCE_IMM, OP_SOURCE_PC,
       OP_TARGET_ADDR, OP_TARGET_ALU_A, OP_TARGET_ALU_B, OP_TARGET_PC, RAM_READ, RAM_WRITE, SOURCE_I,
       SOURCE_J, SOURCE_K, TARGET_I, TARGET_J, TARGET_K;
  wire [5:0] counter_1_out, not_1_out;
  wire [7:0] ROM_VALUE;
  wire [31:0] alu_32_1_dout, DIN, DRAM_d, RAM_ADDR, REG_I_q, REG_J_q, REG_K, ROM_ADDR;
  wire [34:0] IMM_35;

  Seven_Seg_Hex seven_seg_hex_1 (.d(ROM_ADDR[31:28]), .dp(1'b0));
  Seven_Seg_Hex seven_seg_hex_2 (.d(ROM_ADDR[23:20]), .dp(1'b0));
  Seven_Seg_Hex seven_seg_hex_3 (.d(ROM_ADDR[15:12]), .dp(1'b0));
  Seven_Seg_Hex seven_seg_hex_4 (.d(ROM_ADDR[7:4]), .dp(1'b0));
  op_decode_32 op_decode_32_1 (
    .CLK(CLK), .OP_CODE(ROM_VALUE), .TEST(ALU_TEST),
    .OP_SOURCE({SOURCE_K, SOURCE_J, SOURCE_I, OP_SOURCE_ALU, OP_SOURCE_IMM, RAM_READ, OP_SOURCE_ADDR, OP_SOURCE_PC}),
    .OP_TARGET({TARGET_K, TARGET_J, TARGET_I, OP_TARGET_ALU_B, OP_TARGET_ALU_A, RAM_WRITE, OP_TARGET_ADDR, OP_TARGET_PC}),
    .IMM_35(IMM_35), .OP_ISIMM(OP_IS_IMM));
  Seven_Seg_Hex seven_seg_hex_5 (.d(ROM_ADDR[27:24]), .dp(1'b0));
  Seven_Seg_Hex seven_seg_hex_6 (.d(ROM_ADDR[19:16]), .dp(1'b0));
  Seven_Seg_Hex seven_seg_hex_7 (.d(ROM_ADDR[11:8]), .dp(1'b0));
  Seven_Seg_Hex seven_seg_hex_8 (.d(ROM_ADDR[3:0]), .dp(1'b0));
  // Probe DATA_BUS on DIN
  // Probe IMM_35 on IMM_35
  CounterPreset #(.Bits(32), .isProgramCounter("true")) CNT_PC (
    .en(1'b1), .C(CLK), .dir(1'b0), .in(DIN), .ld(OP_TARGET_PC), .clr(1'b0), .out(ROM_ADDR));  // open: ovf
  Register #(.Bits(32)) REG_ADDR (.D(DIN), .C(CLK), .en(OP_TARGET_ADDR), .Q(RAM_ADDR));
  alu_32 alu_32_1 (
    .ALU_OP(IMM_35), .DIN(DIN), .CLK(CLK), .WRITE_A(OP_TARGET_ALU_A), .WRITE_B(OP_TARGET_ALU_B),
    .X({32{1'b0}}), .Y({32{1'b0}}), .SENSE(1'b0), .DOUT(alu_32_1_dout), .TEST(ALU_TEST));
  Seven_Seg_Hex seven_seg_hex_9 (.d(REG_K[31:28]), .dp(1'b0));
  Seven_Seg_Hex seven_seg_hex_10 (.d(REG_K[23:20]), .dp(1'b0));
  Seven_Seg_Hex seven_seg_hex_11 (.d(REG_K[15:12]), .dp(1'b0));
  Seven_Seg_Hex seven_seg_hex_12 (.d(REG_K[7:4]), .dp(1'b0));
  Break break_1 (.brk(OP_TARGET_PC));
  Break break_2 (.brk(OP_TARGET_ADDR));
  Break break_3 (.brk(RAM_WRITE));
  Break break_4 (.brk(OP_TARGET_ALU_A));
  Break break_5 (.brk(OP_TARGET_ALU_B));
  Break break_6 (.brk(TARGET_I));
  Break break_7 (.brk(TARGET_J));
  Break break_8 (.brk(TARGET_K));
  assign DIN = OP_SOURCE_IMM ? IMM_35[31:0] : 32'bz;  // Driver driver_1
  assign DIN = OP_SOURCE_PC ? ROM_ADDR : 32'bz;  // Driver driver_2
  assign DIN = OP_SOURCE_ADDR ? RAM_ADDR : 32'bz;  // Driver driver_3
  assign DIN = OP_SOURCE_ALU ? alu_32_1_dout : 32'bz;  // Driver driver_4
  Seven_Seg_Hex seven_seg_hex_13 (.d(REG_K[27:24]), .dp(1'b0));
  Seven_Seg_Hex seven_seg_hex_14 (.d(REG_K[19:16]), .dp(1'b0));
  Seven_Seg_Hex seven_seg_hex_15 (.d(REG_K[11:8]), .dp(1'b0));
  Seven_Seg_Hex seven_seg_hex_16 (.d(REG_K[3:0]), .dp(1'b0));
  // Probe ROM_ADDR on ROM_ADDR
  // Probe RAM_ADDR on RAM_ADDR
  // Probe ALU_RES on alu_32_1_dout
  Seven_Seg_Hex seven_seg_hex_17 (.d(DIN[31:28]), .dp(1'b0));
  Seven_Seg_Hex seven_seg_hex_18 (.d(DIN[23:20]), .dp(1'b0));
  Seven_Seg_Hex seven_seg_hex_19 (.d(DIN[15:12]), .dp(1'b0));
  Seven_Seg_Hex seven_seg_hex_20 (.d(DIN[7:4]), .dp(1'b0));
  Break break_9 (.brk(OP_SOURCE_PC));
  Break break_10 (.brk(OP_SOURCE_ADDR));
  Break break_11 (.brk(RAM_READ));
  Break break_12 (.brk(OP_SOURCE_IMM));
  Break break_13 (.brk(OP_SOURCE_ALU));
  Break break_14 (.brk(SOURCE_I));
  Break break_15 (.brk(SOURCE_J));
  Break break_16 (.brk(SOURCE_K));
  Seven_Seg_Hex seven_seg_hex_21 (.d(DIN[27:24]), .dp(1'b0));
  Seven_Seg_Hex seven_seg_hex_22 (.d(DIN[19:16]), .dp(1'b0));
  Seven_Seg_Hex seven_seg_hex_23 (.d(DIN[11:8]), .dp(1'b0));
  Seven_Seg_Hex seven_seg_hex_24 (.d(DIN[3:0]), .dp(1'b0));
  and and_1 (and_1_out, ~OP_IS_IMM, OP_SOURCE_PC, OP_TARGET_PC);  // And
  Break SINGLE_STEP (.brk(CLK));
  RAMDualPort #(.AddrBits(24), .Bits(32)) DRAM (
    .A(RAM_ADDR[23:0]), .Din(DIN), .str(RAM_WRITE), .C(CLK), .ld(1'b1), .D(DRAM_d));
  ROM #(.bigEndian("true"), .AddrBits(24), .isProgramMemory("true"), .Bits(8)) IROM (
    .A(ROM_ADDR[23:0]), .sel(1'b1), .D(ROM_VALUE));
  Break HALTED (.brk(and_1_out));
  // Probe RAM_READ on DRAM_d
  // Probe INSTR on ROM_VALUE
  Seven_Seg_Hex seven_seg_hex_25 (.d(IMM_35[31:28]), .dp(1'b0));
  Seven_Seg_Hex seven_seg_hex_26 (.d(IMM_35[23:20]), .dp(1'b0));
  Seven_Seg_Hex seven_seg_hex_27 (.d(IMM_35[15:12]), .dp(1'b0));
  Seven_Seg_Hex seven_seg_hex_28 (.d(IMM_35[7:4]), .dp(1'b0));
  // Probe CLK_COUNT on CLK
  assign DIN = RAM_READ ? DRAM_d : 32'bz;  // Driver driver_5
  Seven_Seg_Hex seven_seg_hex_29 (.d(IMM_35[27:24]), .dp(1'b0));
  Seven_Seg_Hex seven_seg_hex_30 (.d(IMM_35[19:16]), .dp(1'b0));
  Seven_Seg_Hex seven_seg_hex_31 (.d(IMM_35[11:8]), .dp(1'b0));
  Seven_Seg_Hex seven_seg_hex_32 (.d(IMM_35[3:0]), .dp(1'b0));
  and and_2 (and_2_out, TARGET_K, SOURCE_K);
  Counter #(.Bits(6)) counter_1 (.en(TARGET_K), .C(CLK), .clr(and_2_out), .out(counter_1_out));  // open: ovf
  Register #(.Bits(32)) REG_I (.D(DIN), .C(CLK), .en(TARGET_I), .Q(REG_I_q));
  Register #(.Bits(32)) REG_J (.D(DIN), .C(CLK), .en(TARGET_J), .Q(REG_J_q));
  Register #(.Bits(32)) u_REG_K (.D(DIN), .C(CLK), .en(TARGET_K), .Q(REG_K));
  assign not_1_out = ~counter_1_out;  // Not not_1, 6 bits wide
  assign DIN = SOURCE_I ? REG_I_q : 32'bz;  // Driver driver_6
  assign DIN = SOURCE_J ? REG_J_q : 32'bz;  // Driver driver_7
  assign DIN = SOURCE_K ? REG_K : 32'bz;  // Driver driver_8
  LedMatrix #(.colAddrBits(6), .rowDataBits(32), .ledPersistence("true")) ledmatrix_1 (
    .rows({REG_K[0], REG_K[1], REG_K[2], REG_K[3], REG_K[4], REG_K[5], REG_K[6], REG_K[7], REG_K[8], REG_K[9], REG_K[10], REG_K[11], REG_K[12], REG_K[13], REG_K[14], REG_K[15], REG_K[16], REG_K[17], REG_K[18], REG_K[19], REG_K[20], REG_K[21], REG_K[22], REG_K[23], REG_K[24], REG_K[25], REG_K[26], REG_K[27], REG_K[28], REG_K[29], REG_K[30], REG_K[31]}),
    .column(not_1_out));

  // Other names for the same wires on the sheet: DOUT[31:0] = DIN

  // Notes on the sheet:
  //   CLK: Hz: 2147483647
  //   Instruction decoder
  //   Bus
  //   PC
  //   K
  //   Bus target enables
  //   BUS
  //   Bus source enables
  //   Control
  //   RAM
  //   ROM
  //   IROM loads output.bin
  //   IMM
  //   General-purpose register & display output
endmodule
