// Digital circuit mcpu_soc_sliced.dig as structural Verilog
module mcpu_soc_sliced (
  input  SENSE,
  input  CLK
);

  wire and_1_out, IMM7, IMM8, IMM9, IMM10, mcpu_core_slice_1_p9, mcpu_core_slice_1_p25,
       mcpu_core_slice_1_p26, mcpu_core_slice_1_p27, mcpu_core_slice_1_p28, mcpu_core_slice_1_p29,
       mcpu_core_slice_1_p30, mcpu_core_slice_1_p31, mcpu_core_slice_1_p32, mcpu_core_slice_2_p9,
       mcpu_core_slice_2_p25, mcpu_core_slice_2_p26, mcpu_core_slice_2_p27, mcpu_core_slice_2_p28,
       mcpu_core_slice_2_p29, mcpu_core_slice_2_p30, mcpu_core_slice_2_p31, mcpu_core_slice_3_p9,
       mcpu_core_slice_3_p25, mcpu_core_slice_3_p26, mcpu_core_slice_3_p27, mcpu_core_slice_3_p28,
       mcpu_core_slice_3_p29, mcpu_core_slice_3_p30, mcpu_core_slice_3_p31, mcpu_core_slice_4_p25,
       mcpu_core_slice_4_p26, mcpu_core_slice_4_p27, mcpu_core_slice_4_p28, mcpu_core_slice_4_p29,
       multiplexer_1_out, not_1_out, OP_IS_IMM, OP_SOURCE_ADDR, OP_SOURCE_ALU, OP_SOURCE_IMM, OP_SOURCE_PC,
       OP_TARGET_ADDR, OP_TARGET_ALU_A, OP_TARGET_ALU_B, OP_TARGET_PC, RAM_READ, RAM_WRITE, SOURCE_I,
       TARGET_I, TEST;
  wire [3:0] DIN, DOUT;
  wire [6:0] ALU_OP;
  wire [7:6] op_decode_32_1_op_source, op_decode_32_1_op_target;
  wire [34:11] op_decode_32_1_imm_35;

  op_decode_32 op_decode_32_1 (
    .CLK(CLK), .TEST(TEST),
    .OP_SOURCE({op_decode_32_1_op_source, SOURCE_I, OP_SOURCE_ALU, OP_SOURCE_IMM, RAM_READ, OP_SOURCE_ADDR, OP_SOURCE_PC}),
    .OP_TARGET({op_decode_32_1_op_target, TARGET_I, OP_TARGET_ALU_B, OP_TARGET_ALU_A, RAM_WRITE, OP_TARGET_ADDR, OP_TARGET_PC}),
    .IMM_35({op_decode_32_1_imm_35, IMM10, IMM9, IMM8, IMM7, ALU_OP}));  // open: OP_CODE, OP_ISIMM
  Break break_1 (.brk(OP_TARGET_PC));
  Break break_2 (.brk(OP_TARGET_ADDR));
  Break break_3 (.brk(RAM_WRITE));
  Break break_4 (.brk(OP_TARGET_ALU_A));
  Break break_5 (.brk(OP_TARGET_ALU_B));
  Break break_6 (.brk(TARGET_I));
  // mcpu_core_slice mcpu_core_slice_1: pin names not known; wires that end beside it: 1'b1, ALU_OP[4], 1'b0, 1'b0, 1'b0, 1'b1, 1'b0, 1'b0, mcpu_core_slice_1_p9, DIN[0], ALU_OP[0], ALU_OP, 1'b0, 1'b0, IMM7, OP_SOURCE_PC, OP_SOURCE_ADDR, OP_SOURCE_IMM, OP_SOURCE_ALU, OP_TARGET_PC, OP_TARGET_ADDR, OP_TARGET_ALU_A, OP_TARGET_ALU_B, CLK, mcpu_core_slice_1_p25, mcpu_core_slice_1_p26, mcpu_core_slice_1_p27, mcpu_core_slice_1_p28, mcpu_core_slice_1_p29, mcpu_core_slice_1_p30, mcpu_core_slice_1_p31, mcpu_core_slice_1_p32, DOUT[0]
  Break break_7 (.brk(OP_SOURCE_PC));
  Break break_8 (.brk(OP_SOURCE_ADDR));
  Break break_9 (.brk(RAM_READ));
  Break break_10 (.brk(OP_SOURCE_IMM));
  Break break_11 (.brk(OP_SOURCE_ALU));
  Break break_12 (.brk(SOURCE_I));
  // mcpu_core_slice mcpu_core_slice_2: pin names not known; wires that end beside it: mcpu_core_slice_1_p25, mcpu_core_slice_1_p26, mcpu_core_slice_1_p27, mcpu_core_slice_1_p28, mcpu_core_slice_1_p29, mcpu_core_slice_1_p30, mcpu_core_slice_1_p31, mcpu_core_slice_1_p32, mcpu_core_slice_2_p9, DIN[1], ALU_OP[1], ALU_OP, 1'b0, 1'b0, IMM8, OP_SOURCE_PC, OP_SOURCE_ADDR, OP_SOURCE_IMM, OP_SOURCE_ALU, OP_TARGET_PC, OP_TARGET_ADDR, OP_TARGET_ALU_A, OP_TARGET_ALU_B, CLK, mcpu_core_slice_2_p25, mcpu_core_slice_2_p26, mcpu_core_slice_2_p27, mcpu_core_slice_2_p28, mcpu_core_slice_2_p29, mcpu_core_slice_2_p30, mcpu_core_slice_2_p31, mcpu_core_slice_1_p9, DOUT[1]
  Break SINGLE_STEP (.brk(CLK));
  and and_1 (and_1_out, ~OP_IS_IMM, OP_SOURCE_PC, OP_TARGET_PC);  // And
  Break HALTED (.brk(and_1_out));
  // mcpu_core_slice mcpu_core_slice_3: pin names not known; wires that end beside it: mcpu_core_slice_2_p25, mcpu_core_slice_2_p26, mcpu_core_slice_2_p27, mcpu_core_slice_2_p28, mcpu_core_slice_2_p29, mcpu_core_slice_2_p30, mcpu_core_slice_2_p31, mcpu_core_slice_1_p9, mcpu_core_slice_3_p9, DIN[2], ALU_OP[2], ALU_OP, 1'b0, 1'b0, IMM9, OP_SOURCE_PC, OP_SOURCE_ADDR, OP_SOURCE_IMM, OP_SOURCE_ALU, OP_TARGET_PC, OP_TARGET_ADDR, OP_TARGET_ALU_A, OP_TARGET_ALU_B, CLK, mcpu_core_slice_3_p25, mcpu_core_slice_3_p26, mcpu_core_slice_3_p27, mcpu_core_slice_3_p28, mcpu_core_slice_3_p29, mcpu_core_slice_3_p30, mcpu_core_slice_3_p31, mcpu_core_slice_2_p9, DOUT[2]
  // Probe CLK_COUNT on CLK
  // mcpu_core_slice mcpu_core_slice_4: pin names not known; wires that end beside it: mcpu_core_slice_3_p25, mcpu_core_slice_3_p26, mcpu_core_slice_3_p27, mcpu_core_slice_3_p28, mcpu_core_slice_3_p29, mcpu_core_slice_3_p30, mcpu_core_slice_3_p31, mcpu_core_slice_2_p9, 1'b0, DIN[3], ALU_OP[3], ALU_OP, 1'b0, 1'b0, IMM10, OP_SOURCE_PC, OP_SOURCE_ADDR, OP_SOURCE_IMM, OP_SOURCE_ALU, OP_TARGET_PC, OP_TARGET_ADDR, OP_TARGET_ALU_A, OP_TARGET_ALU_B, CLK, mcpu_core_slice_4_p25, mcpu_core_slice_4_p26, mcpu_core_slice_4_p27, mcpu_core_slice_4_p28, mcpu_core_slice_4_p29, mcpu_core_slice_3_p9, DOUT[3]
  Multiplexer #(.Selector_Bits(3)) multiplexer_1 (
    .sel(ALU_OP[2:0]), .in_0(mcpu_core_slice_4_p25), .in_1(mcpu_core_slice_4_p26),
    .in_2(mcpu_core_slice_4_p27), .in_3(mcpu_core_slice_4_p28), .in_4(mcpu_core_slice_4_p29),
    .in_5(mcpu_core_slice_1_p32), .in_6(mcpu_core_slice_3_p9), .in_7(SENSE), .out(multiplexer_1_out));
  not not_1 (not_1_out, multiplexer_1_out);
  Multiplexer multiplexer_2 (.sel(ALU_OP[3]), .in_0(multiplexer_1_out), .in_1(not_1_out), .out(TEST));

  // Other names for the same wires on the sheet: ALU_OP_SEL[2:0] = ALU_OP[2:0]; IMM0 = ALU_OP[0]; IMM1 = ALU_OP[1];
  //   IMM2 = ALU_OP[2]; IMM3 = ALU_OP[3]; IMM4 = ALU_OP[4]

  // Notes on the sheet:
  //   CLK: Hz: 2147483647
  //   Instruction decoder
  //   IMM/ALU OP
  //   Bus target enables
  //   Bus source enables
  //   Control
endmodule
