// Digital circuit op_decode_32.dig as structural Verilog
module op_decode_32 (
  input  CLK,
  input  [7:0] OP_CODE,
  input  TEST,
  output [7:0] OP_SOURCE,
  output [7:0] OP_TARGET,
  output [34:0] IMM_35,
  output OP_ISIMM
);

  wire and_1_out, and_2_out, and_3_out, FLAG_LASTIMM_nq, not_1_out, or_1_out;
  wire [7:0] decoder_1_out_0, decoder_2_out_0;

  and and_1 (and_1_out, OP_CODE[6], TEST);
  D_FF FLAG_LASTIMM (.D(OP_CODE[7]), .C(CLK), .nQ(FLAG_LASTIMM_nq));  // open: Q
  Decoder #(.Selector_Bits(3)) decoder_1 (
    .sel(OP_CODE[2:0]), .out_0(decoder_1_out_0[0]), .out_1(decoder_1_out_0[1]), .out_2(decoder_1_out_0[2]),
    .out_3(decoder_1_out_0[3]), .out_4(decoder_1_out_0[4]), .out_5(decoder_1_out_0[5]),
    .out_6(decoder_1_out_0[6]), .out_7(decoder_1_out_0[7]));
  Decoder #(.Selector_Bits(3)) decoder_2 (
    .sel(OP_CODE[5:3]), .out_0(decoder_2_out_0[0]), .out_1(decoder_2_out_0[1]), .out_2(decoder_2_out_0[2]),
    .out_3(decoder_2_out_0[3]), .out_4(decoder_2_out_0[4]), .out_5(decoder_2_out_0[5]),
    .out_6(decoder_2_out_0[6]), .out_7(decoder_2_out_0[7]));
  or or_1 (or_1_out, ~OP_CODE[6], and_1_out);  // Or
  and and_2 (and_2_out, OP_CODE[7], FLAG_LASTIMM_nq);
  and and_3 (and_3_out, or_1_out, ~OP_CODE[7]);  // And
  Multiplexer #(.Bits(8)) multiplexer_1 (.sel(OP_CODE[7]), .in_0(decoder_1_out_0), .in_1({8{1'b0}}), .out(OP_SOURCE));
  Multiplexer #(.Bits(8)) multiplexer_2 (.sel(not_1_out), .in_0(decoder_2_out_0), .in_1({8{1'b0}}), .out(OP_TARGET));
  not not_1 (not_1_out, and_3_out);
  srg_imm_7x5 SRG_IMM (.clear(and_2_out), .din(OP_CODE[6:0]), .clk(CLK), .ena(OP_CODE[7]), .dout(IMM_35));

  assign OP_ISIMM = OP_CODE[7];
endmodule
