// Digital circuit srg_imm_7x5.dig as structural Verilog
module srg_imm_7x5 (
  input  clear,
  input  [6:0] din,
  input  clk,
  input  ena,
  output [34:0] dout
);

  wire not_1_out;
  wire [6:0] multiplexer_1_out, multiplexer_2_out, multiplexer_3_out, multiplexer_4_out;

  not not_1 (not_1_out, clear);
  Register #(.Bits(7)) register_1 (.D(din), .C(clk), .en(ena), .Q(dout[6:0]));
  Multiplexer #(.Bits(7)) multiplexer_1 (.sel(not_1_out), .in_0({7{1'b0}}), .in_1(dout[6:0]), .out(multiplexer_1_out));
  Register #(.Bits(7)) register_2 (.D(multiplexer_1_out), .C(clk), .en(ena), .Q(dout[13:7]));
  Multiplexer #(.Bits(7)) multiplexer_2 (.sel(not_1_out), .in_0({7{1'b0}}), .in_1(dout[13:7]), .out(multiplexer_2_out));
  Register #(.Bits(7)) register_3 (.D(multiplexer_2_out), .C(clk), .en(ena), .Q(dout[20:14]));
  Multiplexer #(.Bits(7)) multiplexer_3 (
    .sel(not_1_out), .in_0({7{1'b0}}), .in_1(dout[20:14]), .out(multiplexer_3_out));
  Register #(.Bits(7)) register_4 (.D(multiplexer_3_out), .C(clk), .en(ena), .Q(dout[27:21]));
  Multiplexer #(.Bits(7)) multiplexer_4 (
    .sel(not_1_out), .in_0({7{1'b0}}), .in_1(dout[27:21]), .out(multiplexer_4_out));
  Register #(.Bits(7)) register_5 (.D(multiplexer_4_out), .C(clk), .en(ena), .Q(dout[34:28]));
endmodule
